# Fritzing sketch ampli_and_inputs (saved by Fritzing 0.9.2b)
circuit board: 7.45238cm x 6.1078cm
breadboards: 1

parts:
  U2 = TDA2822 [part_number=TDA2822 package=dip08]
  C1 = Electrolytic Capacitor [capacitance=470µF package="100 mil [THT, electrolytic]"]
  C2 = Ceramic Capacitor [capacitance=100nF package="100 mil [THT, multilayer]"]
  R1 = Resistor [tolerance=±5% resistance=4.7 package=THT]
  C3 = Electrolytic Capacitor [capacitance=10µF package="100 mil [THT, electrolytic]"]
  C4 = Electrolytic Capacitor [capacitance=100µF package="100 mil [THT, electrolytic]"]
  R4 = Resistor [tolerance=±5% resistance=10k package=THT]
  U1 = OP37 - Low Noise, Precision, High Speed Op Amp [part_number=MC1741]
  AudioOut = AUDIO-JACK2 [package=audio-jack]
  SP1 = SPEAKER [package=pcb_mount_speaker]
  R5 = Resistor [tolerance=±5% resistance=499k package=THT]
  R6 = Resistor [tolerance=±5% resistance=3.9k package=THT]
  C5 = Ceramic Capacitor [capacitance=4.7nF package="100 mil [THT, multilayer]"]
  R7 = Resistor [tolerance=±5% resistance=270 package=THT]
  C6 = Ceramic Capacitor [capacitance=100nF package="100 mil [THT, multilayer]"]
  S1 = Toggle Switch [package=THT]
  MIC2 = Microphone
  R8 = Resistor [tolerance=±5% resistance=10k package=THT]
  R9 = Resistor [tolerance=±5% resistance=10k package=THT]
  C7 = Ceramic Capacitor [capacitance=100nF package="100 mil [THT, multilayer]"]
  C8 = Ceramic Capacitor [capacitance=100nF package="100 mil [THT, multilayer]"]
  Q2 = NPN-Transistor [package="TO92 [THT]"]
  R10 = Resistor [tolerance=±5% resistance=100k package=THT]
  J1 = mini DIN 6 Connector [package=mini-din6]
  R3 = Resistor [tolerance=±5% resistance=10k package=THT]
  Arduino = Arduino Uno (Rev3)
  R2 = Rotary Potentiometer (Large) [maximum_resistance=100kΩ package=THT]

nets (from the pcb view):
  N1: U2.A_OUT, C1.+
  VCC: U2.Vcc, C3.+, U1.V+, Arduino.VIN
  N2: U2.GND, R1.Pin_0, C3.-, C4.-, R4.Pin_1, U1.-V, AudioOut.SLEEVE, SP1.+, C5.1, C6.0, S1.L1, R2.leg2
  N3: U2.A_-IN, R2.wiper
  N4: U2.A_IN, C4.+
  N5: C1.-, C2.1, AudioOut.RING, AudioOut.TIP
  N6: C2.0, R1.Pin_1
  N7: R4.Pin_0, U1.-IN, R3.Pin_0
  N8: U1.+IN, R7.Pin_1, C6.1
  N9: U1.OUT, R3.Pin_1, R2.leg1
  N10: AudioOut.RSH, AudioOut.TSH, SP1.-
  N11: R5.Pin_0, Arduino.D10_PWM/SS
  N12: R5.Pin_1, R6.Pin_1, C5.0, R7.Pin_0
  N13: R6.Pin_0, Arduino.D9_PWM
  GND: S1.COM, MIC2.pin1, Q2.E, J1.GND, Arduino.GND
  N14: MIC2.pin2, R9.Pin_1, C8.1
  N15: R8.Pin_0, R9.Pin_0, Arduino.3V3
  N16: R8.Pin_1, C7.1, Q2.C, R10.Pin_0
  N17: C7.0, Arduino.A0
  N18: C8.0, Q2.B, R10.Pin_1
  N19: J1.Data, Arduino.D4
  VCC_2: J1.Vcc, Arduino.5V
  N20: J1.Clock, Arduino.D3_PWM

notes:
  Ampli 2
  Ampli 1
  Output
  Microphone
  Filter
  Keyboard input

custom parts:
  TDA2822: dual OP Amp
  mini DIN 6 Connector: mini DIN 6 Connector Commonly found on the back of a computer for PS2 keyboard and mice. Schematic and footprint are proven. Spark Fun Electronics SKU : PRT-08509
